# Fritzing sketch wiring (saved by Fritzing 1.0.0rc)
breadboards: 1

parts:
  Bauteil3 = Adafruit T-Cobbler Plus [part_number="Adafruit #1989 and #2028"]
  part = Resistor [tolerance=±5% resistance=68 power=0.25W package=THT]
  LED = LED - 3mm [color="Red (633nm)" current=0.030A package="3 mm [THT]"]
  Button1 = Pushbutton [package="[THT]"]
  R2 = Resistor [tolerance=±5% resistance=10k power=0.25W package=THT]

nets:
  N1: Bauteil3.+3.3V, Button1.Pin_1, Button1.Pin_2
  N2: Bauteil3.GND, part.Pin_0
  N3: Bauteil3.GPIO22, LED.anode
  N4: Bauteil3.GPIO24, R2.Pin_1
  N5: part.Pin_1, LED.cathode
  N6: Button1.Pin_3, Button1.Pin_4, R2.Pin_0

custom parts:
  Adafruit T-Cobbler Plus: The Raspberry Pi has landed on the Maker World like a 40-GPIO pinned, quad-USB ported, credit card sized bomb of DIY joy. And while you can use most of our great Model B accessories by hooking up our downgrade cable, its probably a good time to upgrade your set up and accessorize using all of the 40 pins. That's why we now carry the Assembled Adafruit Pi T-Cobbler Plus - Breakout + Cable for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
